// Logisim project cpu1.circ as structural Verilog: 6 circuits, main circuit main
module main (
  input  in_1,
  input  in_2,
  input  in_3,
  input  in_4
);

  wire and_1_out, and_2_out, button_1_out, button_2_out, controlled_buffer_1_out;

  and and_1 (and_1_out, in_1, in_2);
  and and_2 (and_2_out, in_3, in_4);
  assign controlled_buffer_1_out = button_1_out ? and_1_out : 1'bz;  // Controlled_Buffer controlled_buffer_1
  assign controlled_buffer_1_out = button_2_out ? and_2_out : 1'bz;  // Controlled_Buffer controlled_buffer_2
  Button button_1 (.out(button_1_out));
  Button button_2 (.out(button_2_out));
endmodule

module memory_1 (
  input  s,
  input  e,
  output q
);

  wire nand_1_out, nand_2_out, nand_4_out;

  nand nand_1 (nand_1_out, s, e);
  nand nand_2 (nand_2_out, nand_1_out, e);
  nand nand_3 (q, nand_1_out, nand_4_out);
  nand nand_4 (nand_4_out, q, nand_2_out);

  // Notes on the sheet:
  //   1 bit memory cell
endmodule

module memory_8 (
  input  [7:0] in_1,
  input  in_2,
  output [7:0] out_3
);

  memory_1 memory_1_1 (.s(in_1[0]), .e(in_2), .q(out_3[0]));
  memory_1 memory_1_2 (.s(in_1[1]), .e(in_2), .q(out_3[1]));
  memory_1 memory_1_3 (.s(in_1[2]), .e(in_2), .q(out_3[2]));
  memory_1 memory_1_4 (.s(in_1[3]), .e(in_2), .q(out_3[3]));
  memory_1 memory_1_5 (.s(in_1[4]), .e(in_2), .q(out_3[4]));
  memory_1 memory_1_6 (.s(in_1[5]), .e(in_2), .q(out_3[5]));
  memory_1 memory_1_7 (.s(in_1[6]), .e(in_2), .q(out_3[6]));
  memory_1 memory_1_8 (.s(in_1[7]), .e(in_2), .q(out_3[7]));
endmodule

module cpu_enable (
  input  [7:0] I,
  input  E,
  output [7:0] O
);

  and and_1 (O[0], I[0], E);
  and and_2 (O[1], I[1], E);
  and and_3 (O[2], I[2], E);
  and and_4 (O[3], I[3], E);
  and and_5 (O[4], I[4], E);
  and and_6 (O[5], I[5], E);
  and and_7 (O[6], I[6], E);
  and and_8 (O[7], I[7], E);
endmodule

module cpu_reg_8 (
  input  [7:0] in_1,
  input  s,
  input  e,
  output [7:0] out_4,
  output [7:0] out_5
);

  wire [7:0] cpu_enable_1_o;

  memory_8 memory_8_1 (.in_1(in_1), .out_3(out_4), .in_2(s));
  cpu_enable cpu_enable_1 (.I(out_4), .E(e), .O(cpu_enable_1_o));
  assign out_5[0] = e ? cpu_enable_1_o[0] : 1'bz;  // Controlled_Buffer controlled_buffer_1
  // Pins of 1 and 8 bits meet at out_5
  // Pins of 1 and 8 bits meet at cpu_enable_1_o
endmodule

module cpu_reg_byte (
  input  [6:0] in_1,
  input  in_2,
  input  h,
  input  v,
  input  s,
  input  e
);

  wire and_1_out, and_2_out, and_3_out, or_1_out;
  wire [7:0] cpu_reg_8_1_out_5;
  wire [7:7] undriven;

  and and_1 (and_1_out, h, v);
  and and_2 (and_2_out, and_1_out, s);
  and and_3 (and_3_out, and_1_out, e);
  or or_1 (or_1_out, in_2, and_2_out);
  cpu_reg_8 cpu_reg_8_1 (
    .in_1({undriven[7], in_1}), .s(or_1_out), .e(and_3_out), .out_5(cpu_reg_8_1_out_5));  // open: out_4
  // Pins of 7 and 8 bits meet at {undriven[7], in_1}
endmodule
